# Fritzing sketch SMLReader (saved by Fritzing 0.9.5d)

parts:
  WeMos_D1_Mini1 = WeMos D1 Mini
  Q1 = LTR-301 [package=ltr-301]
  R1 = Resistor [tolerance=±5% resistance=1k package="2010 [SMD]"]

nets:
  N1: WeMos_D1_Mini1.3V3, R1.Pin_0
  N2: WeMos_D1_Mini1.D2, Q1.E, R1.Pin_1
  N3: WeMos_D1_Mini1.G, Q1.C

notes:
  1kΩ
  BPW 40
  Collector (flache Seite)
  Emitter
